# Fritzing sketch Desenho Placa Estação Meteorológica (saved by Fritzing 0.9.2b)
circuit board: 15cm x 10cm
breadboards: 1

parts:
  DHT4 = DHT11 Humitidy and Temperature Sensor
  T3 = LM35 Temperature Sensor [package="TO92 [THT]"]
  Componente7 = Barometric Pressure Sensor - BMP180 Breakout (GY-68)
  DHT5 = DHT11 Humitidy and Temperature Sensor
  R5 = Resistor [tolerance=±5% resistance=220 package=THT]
  Componente8 = Arduino Uno (Rev3)
  R6 = Resistor [tolerance=±5% resistance=220 package=THT]
  GLCD_84x3 = 84 x 48 Graphic LCD

nets:
  VDD: DHT4.VDD, T3.+Vs, DHT5.VDD, R5.Pin_0, Componente8.5V
  N1: DHT4.DATA, R5.Pin_1, Componente8.D2
  GND: DHT4.GND, T3.GND, Componente7.GND, DHT5.GND, Componente8.GND, GLCD_84x3.8_GND
  N2: T3.Vout, Componente8.A0
  VCC: Componente7.VCC, Componente8.3V3
  N3: Componente7.SCL, Componente8.A5/SCL
  N4: Componente7.SDA, Componente8.A4/SDA
  N5: DHT5.DATA, Componente8.A2
  N6: Componente8.D8, GLCD_84x3.5_CLK
  N7: Componente8.D9_PWM, GLCD_84x3.4_DIN
  N8: Componente8.D10_PWM/SS, GLCD_84x3.3_DC
  N9: Componente8.D11_PWM/MOSI, GLCD_84x3.2_CE
  N10: Componente8.D12/MISO, GLCD_84x3.1_RST
  N11: R6.Pin_0, GLCD_84x3.6_VCC
  N12: R6.Pin_1, GLCD_84x3.7_LIGHT

custom parts:
  DHT11 Humitidy and Temperature Sensor: DHT11 Humidity and Temperature Sensor
